// Logisim project a1-comp2731.circ as structural Verilog: 7 circuits, main circuit main
module main (
  input  [2:0] A,
  input  [2:0] B,
  output [1:0] H,
  output [2:0] S,
  output [2:0] out_5
);

  wire and_1_out, and_2_out, and_3_out, and_4_out, and_5_out, greater_than_checker_1_out_7,
       h_checker_1_out_3, n3bit_subtractor_1_out_7, n3bit_subtractor_1_out_8, n3bit_subtractor_1_out_9,
       not_1_out, or_1_out, xor_2_out_3, xor_3_out_3, xor_4_out_3, xor_5_out_3;

  H_checker h_checker_1 (.in_1(H[1]), .in_2(H[0]), .out_3(h_checker_1_out_3));
  \xor  xor_1 (.in_1(and_2_out), .in_2(xor_5_out_3), .out_3(H[0]));
  \xor  xor_2 (.in_1(A[0]), .in_2(B[0]), .out_3(xor_2_out_3));
  \xor  xor_3 (.in_1(A[1]), .in_2(B[1]), .out_3(xor_3_out_3));
  \xor  xor_4 (.in_1(A[2]), .in_2(B[2]), .out_3(xor_4_out_3));
  greater_than_checker greater_than_checker_1 (
    .a0(A[0]), .a1(A[1]), .a2(A[2]), .b0(B[0]), .b1(B[1]), .b2(B[2]), .out_7(greater_than_checker_1_out_7));
  not not_1 (not_1_out, and_1_out);
  and and_1 (and_1_out, h_checker_1_out_3, greater_than_checker_1_out_7);
  _3bit_subtractor u_3bit_subtractor_1 (
    .in_1(B[2]), .in_2(A[2]), .in_3(B[1]), .in_4(A[1]), .in_5(B[0]), .in_6(A[0]),
    .out_7(n3bit_subtractor_1_out_7), .out_8(n3bit_subtractor_1_out_8), .out_9(n3bit_subtractor_1_out_9),
    .out_10(out_5));
  \xor  xor_5 (.in_1(or_1_out), .in_2(H[1]), .out_3(xor_5_out_3));
  multiplexor multiplexor_1 (
    .in_1(n3bit_subtractor_1_out_9), .in_7(not_1_out), .out_8(S[0]), .in_3(n3bit_subtractor_1_out_8),
    .in_4(H[1]), .in_6(1'b0), .in_2(H[0]), .out_9(S[1]), .in_5(n3bit_subtractor_1_out_7), .out_10(S[2]));
  and and_2 (and_2_out, xor_2_out_3, xor_4_out_3, xor_3_out_3);
  or or_1 (or_1_out, xor_2_out_3, xor_4_out_3, xor_3_out_3);
  and and_3 (and_3_out, xor_2_out_3, xor_3_out_3);
  and and_4 (and_4_out, xor_3_out_3, xor_4_out_3);
  or or_2 (H[1], and_3_out, and_5_out, and_4_out);
  and and_5 (and_5_out, xor_2_out_3, xor_4_out_3);

  // Notes on the sheet:
  //   MAIN CIRCUIT
endmodule

module \xor  (
  input  in_1,
  input  in_2,
  output out_3
);

  wire and_1_out, and_2_out, not_1_out, not_2_out;

  not not_1 (not_1_out, in_2);
  not not_2 (not_2_out, in_1);
  and and_1 (and_1_out, in_1, not_1_out);
  and and_2 (and_2_out, not_2_out, in_2);
  or or_1 (out_3, and_1_out, and_2_out);

  // Notes on the sheet:
  //   XOR 1 input
endmodule

module greater_than_checker (
  input  a0,
  input  a1,
  input  a2,
  input  b0,
  input  b1,
  input  b2,
  output out_7
);

  wire and_1_out, and_2_out, and_3_out, not_1_out, not_2_out, not_3_out, not_4_out, not_5_out, xor_1_out_3,
       xor_2_out_3;

  not not_1 (not_1_out, b1);
  not not_2 (not_2_out, b2);
  \xor  xor_1 (.in_1(a2), .in_2(b2), .out_3(xor_1_out_3));
  not not_3 (not_3_out, xor_1_out_3);
  and and_1 (and_1_out, a2, not_2_out);
  \xor  xor_2 (.in_1(b1), .in_2(a1), .out_3(xor_2_out_3));
  not not_4 (not_4_out, xor_2_out_3);
  and and_2 (and_2_out, a0, not_4_out, not_3_out, not_5_out);
  not not_5 (not_5_out, b0);
  and and_3 (and_3_out, a1, not_1_out, not_3_out);
  or or_1 (out_7, and_2_out, and_3_out, and_1_out);

  // Notes on the sheet:
  //   A>B?
endmodule

module H_checker (
  input  in_1,
  input  in_2,
  output out_3
);

  wire and_1_out, and_2_out, not_1_out, not_2_out;

  not not_1 (not_1_out, in_1);
  and and_1 (and_1_out, not_1_out, in_2);
  not not_2 (not_2_out, in_2);
  and and_2 (and_2_out, not_1_out, not_2_out);
  or or_1 (out_3, and_1_out, and_1_out, and_2_out, and_2_out, and_2_out);

  // Notes on the sheet:
  //   H<2?
endmodule

module multiplexor (
  input  in_1,
  input  in_2,
  input  in_3,
  input  in_4,
  input  in_5,
  input  in_6,
  input  in_7,
  output out_8,
  output out_9,
  output out_10
);

  wire and_1_out, and_2_out, and_3_out, and_4_out, and_5_out, and_6_out, not_1_out;

  not not_1 (not_1_out, in_7);
  and and_1 (and_1_out, in_1, not_1_out);
  and and_2 (and_2_out, in_2, in_7);
  and and_3 (and_3_out, in_3, not_1_out);
  and and_4 (and_4_out, in_4, in_7);
  and and_5 (and_5_out, not_1_out, in_5);
  and and_6 (and_6_out, in_6, in_7);
  or or_1 (out_8, and_1_out, and_2_out);
  or or_2 (out_9, and_3_out, and_4_out);
  or or_3 (out_10, and_5_out, and_6_out);

  // Notes on the sheet:
  //   XOR 3-bit input
endmodule

module full_adder (
  input  in_1,
  input  in_2,
  input  in_3,
  output out_4,
  output out_5
);

  wire and_1_out, and_2_out, xor_1_out_3;

  \xor  xor_1 (.in_1(in_1), .in_2(in_2), .out_3(xor_1_out_3));
  and and_1 (and_1_out, in_1, in_2);
  \xor  xor_2 (.in_1(xor_1_out_3), .in_2(in_3), .out_3(out_4));
  and and_2 (and_2_out, xor_1_out_3, in_3);
  \xor  xor_3 (.in_1(and_1_out), .in_2(and_2_out), .out_3(out_5));

  // Notes on the sheet:
  //   FULL ADDER
endmodule

module _3bit_subtractor (
  input  in_1,
  input  in_2,
  input  in_3,
  input  in_4,
  input  in_5,
  input  in_6,
  output out_7,
  output out_8,
  output out_9,
  output [2:0] out_10
);

  wire full_adder_2_out_5, full_adder_3_out_5, xor_1_out_3, xor_2_out_3, xor_3_out_3;

  \xor  xor_1 (.in_1(1'b1), .in_2(in_1), .out_3(xor_1_out_3));
  full_adder full_adder_1 (.in_1(full_adder_2_out_5), .in_2(in_2), .in_3(xor_1_out_3), .out_4(out_7));  // open: out_5
  full_adder full_adder_2 (
    .in_1(full_adder_3_out_5), .in_2(in_4), .in_3(xor_2_out_3), .out_4(out_8), .out_5(full_adder_2_out_5));
  \xor  xor_2 (.in_1(1'b1), .in_2(in_3), .out_3(xor_2_out_3));
  \xor  xor_3 (.in_1(1'b1), .in_2(in_5), .out_3(xor_3_out_3));
  full_adder full_adder_3 (.in_1(1'b1), .in_2(in_6), .in_3(xor_3_out_3), .out_4(out_9), .out_5(full_adder_3_out_5));

  assign out_10 = {out_7, out_8, out_9};

  // Notes on the sheet:
  //   3-bit Subtractor
endmodule
